# Fritzing sketch Lepton wiring (saved by Fritzing 0.9.3b)

parts:
  IC2 = DIP - 22 pins [chip_label=IC package="DIP (Dual Inline) [THT]"]
  Raspberry_Pi_1 = Raspberry Pi 3 [part_number=RPI-3-V1.2]

nets:
  N1: IC2.pin5, Raspberry_Pi_1.GPIO2
  N2: IC2.pin7, Raspberry_Pi_1.GPIO11
  N3: IC2.pin8, Raspberry_Pi_1.GPIO3
  N4: IC2.pin10, Raspberry_Pi_1.GPIO8
  N5: IC2.pin12, Raspberry_Pi_1.GPIO9
  3V3: IC2.pin15, IC2.pin22, Raspberry_Pi_1.3v3, Raspberry_Pi_1.3V3
  N6: IC2.pin21, Raspberry_Pi_1.GND

custom parts:
  DIP - 22 pins: A DIP stand-in part for whatever IC you want. With 22 pins on a 300mil dual inline package (DIP) footprint.
